# Fritzing sketch robot_wiring_diagram (saved by Fritzing 0.9.3b)
breadboards: 1

parts:
  NRF24L01 = NRF24L01
  PCA9685 = Adafruit PCA9685 PWM/Servo Breakout [part_number=815]
  L298N_#1 = H-Bridge with L298N
  L298N_#2 = H-Bridge with L298N
  Motor_3 = DC Motor
  Raspberry_Pi_Pico = Raspberry Pi Pico or Pico 2
  Motor_1 = DC Motor
  Motor_4 = DC Motor
  Motor_2 = DC Motor
  BAT1 = 12 battery [package=battery]  # not connected

nets:
  VCC: NRF24L01.VCC, PCA9685.VCC, Raspberry_Pi_Pico.pin_36
  5V: PCA9685.PWRIN, L298N_#1.5V, L298N_#2.5V
  GND: PCA9685.GND, L298N_#1.GND, L298N_#2.GND
  N1: L298N_#1.M1-02, Motor_1.pin_1
  N2: L298N_#1.M2-01, Motor_2.pin_2
  N3: L298N_#2.M1-01, Motor_3.pin_2
  N4: L298N_#2.M1-02, Motor_3.pin_1
  N5: L298N_#2.M2-01, Motor_4.pin_2
  N6: L298N_#2.M2-02, Motor_4.pin_1

custom parts:
  Adafruit PCA9685 PWM/Servo Breakout: Using only two pins, control 16 free-running PWM outputs! I2C-controlled PWM driver with a built in clock. Unlike the TLC5940 family, you do not need to continuously send it signal tying up your microcontroller, its completely free running! 5V compliant, which means you can control it from a 3.3V microcontroller and still safely drive up to 6V outputs (this is good for when you want to control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
  H-Bridge with L298N: h-bridge
  Raspberry Pi Pico or Pico 2: Raspberry Pi Pico and Pico 2. Based around the RP2040 and RP2350 microcontrollers respectively, Picos are low cost microcontroller device bringing Raspberry Pi quality, cost, and easy of use to the microcontroller space. Jan 2021, Split part in to two versions: tht (this one) and SMD. This one will drill holes for a .1 in header in pcb to allow plugging in the module as well as providing pads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
  12 battery: 12V lead acid type battery, like the Husqvarna YTH2448 12V 35AH battery. This is the mini version 1/4 the size of the actual battery to be closer to typical breadboard parts (around 2in wide rathher than 7in). The pads in pcb are sized to accomidate up to 14ga wire (as these batterys will deliver high currents.)
